# Fritzing sketch joystick (saved by Fritzing 0.6.3b)
breadboards: 1

parts:
  R1 = Resistor [tolerance=±5% resistance=1.0k package=THT]
  Arduino1 = Arduino
  J1 = female pin header, 8 pins [form="♀ (female)"]
  R2 = Resistor [tolerance=±5% resistance=100k package=THT]
  R3 = Resistor [tolerance=±5% resistance=100k package=THT]
  R5 = Resistor [tolerance=±5% resistance=100k package=THT]
  R6 = Resistor [tolerance=±5% resistance=1.0k package=THT]
  R7 = Rotary Potentiometer (Small) [maximum_resistance=96kΩ]
  R8 = Rotary Potentiometer (Small) [maximum_resistance=96kΩ]
  R9 = Rotary Potentiometer (Small) [maximum_resistance=86kΩ]
  S1 = Pushbutton [package=THT]
  S3 = Pushbutton [package=THT]
  J2 = female pin header, 8 pins [form="♀ (female)"]

nets:
  N1: R1.Pin_0, Arduino1.D2, J1.pin2
  N2: R1.Pin_1, Arduino1.+5V, J1.pin1, R6.Pin_1
  N3: Arduino1.GND, J1.pin4, J1.pin7, R2.Pin_1, R3.Pin_1, R5.Pin_1
  N4: Arduino1.D3, J1.pin6, R6.Pin_0
  N5: Arduino1.A0, J1.pin3, R2.Pin_0
  N6: Arduino1.A1, J1.pin5, R3.Pin_0
  N7: Arduino1.A2, J1.pin8, R5.Pin_0
  N8: R7.wiper, R8.wiper, R9.wiper, J2.pin1
  N9: R7.leg2, J2.pin3
  N10: R8.leg2, J2.pin5
  N11: R9.leg2, J2.pin8
  N12: S1.leg0, J2.pin4
  N13: S1.leg1, J2.pin2
  N14: S3.leg0, J2.pin7
  N15: S3.leg1, J2.pin6
