# Fritzing sketch joystick (saved by Fritzing 0.9.2b)
breadboards: 1

parts:
  R1 = Resistor [tolerance=±5% resistance=1.0k package=THT]
  J1 = female pin header, 8 pins [form="♀ (female)"]
  R2 = Resistor [tolerance=±5% resistance=100k package=THT]
  R3 = Resistor [tolerance=±5% resistance=100k package=THT]
  R5 = Resistor [tolerance=±5% resistance=100k package=THT]
  R6 = Resistor [tolerance=±5% resistance=1.0k package=THT]
  S1 = Pushbutton [package=THT]
  S3 = Pushbutton [package=THT]
  J2 = female pin header, 8 pins [form="♀ (female)"]
  part = female pin header, 8 pins [form="♀ (female)"]  # not connected
  R8 = Rotary Potentiometer (Small) [maximum_resistance=96kΩ package=THT]
  Arduino1 = Arduino Uno (Rev3)
  R9 = Rotary Potentiometer (Small) [maximum_resistance=86kΩ package=THT]
  R7 = Rotary Potentiometer (Small) [maximum_resistance=96kΩ package=THT]

nets:
  N1: R1.Pin_0, J1.pin2, Arduino1.D2
  N2: R1.Pin_1, J1.pin1, R6.Pin_1
  N3: J1.pin3, R2.Pin_0, Arduino1.A0
  N4: J1.pin4, J1.pin7, R2.Pin_1, R3.Pin_1, R5.Pin_1, Arduino1.GND
  N5: J1.pin5, R3.Pin_0, Arduino1.A1
  N6: J1.pin6, R6.Pin_0
  N7: J1.pin8, R5.Pin_0, Arduino1.A2
  N8: S1.leg0, J2.pin4
  N9: S1.leg1, J2.pin2
  N10: S3.leg0, J2.pin7
  N11: S3.leg1, J2.pin6
  N12: J2.pin1, R8.wiper, R9.wiper, R7.wiper
  N13: J2.pin3, R7.leg2
  N14: J2.pin5, R8.leg2
  N15: J2.pin8, R9.leg2
